# Fritzing sketch ventilagon_botonera (saved by Fritzing 0.8.7b)
breadboards: 1

parts:
  U1 = atmega328 [package=dip]
  R1 = Resistor [tolerance=±5% resistance=10k package=THT]
  Raspberry_Pi_B_rev1 = Raspberry Pi B rev1
  R2 = Resistor [tolerance=±5% resistance=3.3k package=THT]
  R3 = Resistor [tolerance=±5% resistance=1.6k package=THT]
  Y1 = CRYSTAL [package=hc49us]
  C1 = Capacitor [package=cap-pth-small]
  C2 = Capacitor [package=cap-pth-small]

nets:
  N1: U1.RESET, R1.Pin_0
  N2: U1.D0_(RX), Raspberry_Pi_B_rev1.GPIO_14
  N3: U1.D1_(TX), R3.Pin_1
  VCC: U1.VCC, R1.Pin_1, Raspberry_Pi_B_rev1.5V
  GND: U1.GND, Raspberry_Pi_B_rev1.GND, R2.Pin_1
  N4: U1.XLAT1, Y1.2, C1.1
  N5: U1.XLAT2, Y1.1, C2.2
  N6: Raspberry_Pi_B_rev1.GPIO_15, R2.Pin_0, R3.Pin_0
